// Logisim project processor-v7.circ as structural Verilog: 4 circuits, main circuit Main
module ALU (
  input  [31:0] OpA,
  input  [31:0] OpB,
  input  [2:0] func3,
  input  func7,
  output [31:0] Res,
  output AluSup,
  output AluEq,
  output AluInf
);

  wire [31:0] adder_1_out, adder_2_out, AND_out, multiplexer_1_out, multiplexer_2_out, not_1_out, OR_out,
       shifter_1_out, shifter_2_out, shifter_3_out, XOR_out;

  assign not_1_out = ~OpB;  // NOT_Gate not_1, 32 bits wide
  Adder #(.width(32)) adder_1 (.a(OpA), .b(OpB), .out(adder_1_out), .cin(1'b0));  // open: cout
  Adder #(.width(32)) adder_2 (.a(OpA), .b(not_1_out), .out(adder_2_out), .cin(1'b1));  // open: cout
  Shifter #(.width(32)) shifter_1 (.in(OpA), .\dist (OpB[4:0]), .out(shifter_1_out));
  Shifter #(.width(32), .shift("lr")) shifter_2 (.in(OpA), .\dist (OpB[4:0]), .out(shifter_2_out));
  Shifter #(.width(32), .shift("ar")) shifter_3 (.in(OpA), .\dist (OpB[4:0]), .out(shifter_3_out));
  assign XOR_out = OpA ^ OpB;  // XOR_Gate XOR, 32 bits wide
  assign OR_out = OpA | OpB;  // OR_Gate OR, 32 bits wide
  assign AND_out = OpA & OpB;  // AND_Gate AND, 32 bits wide
  Comparator #(.width(32)) comparator_1 (.a(OpA), .b(OpB), .gt(AluSup), .eq(AluEq), .lt(AluInf));
  Multiplexer #(.width(32), .enable("false")) multiplexer_1 (
    .in0(adder_1_out), .in1(adder_2_out), .out(multiplexer_1_out), .sel(func7));
  Multiplexer #(.width(32), .enable("false")) multiplexer_2 (
    .in0(shifter_2_out), .in1(shifter_3_out), .out(multiplexer_2_out), .sel(func7));
  Multiplexer #(.select(3), .width(32), .enable("false")) multiplexer_3 (
    .in0(multiplexer_1_out), .in1(shifter_1_out), .in4(XOR_out), .in5(multiplexer_2_out), .in6(OR_out),
    .in7(AND_out), .out(Res), .sel(func3));  // open: in2, in3
endmodule

// Register File
module RegisterFile (
  input  Clock,
  input  [31:0] RFIn,
  input  [4:0] SelOpA,
  input  [4:0] SelOpB,
  input  [4:0] SelDest,
  output [31:0] RFOpA,
  output [31:0] RFOpB,
  output [31:0] _0x00,
  output [31:0] _0x01,
  output [31:0] _0x02,
  output [31:0] _0x03,
  output [31:0] _0x04,
  output [31:0] _0x05,
  output [31:0] _0x06,
  output [31:0] _0x07,
  output [31:0] _0x08,
  output [31:0] _0x09,
  output [31:0] _0x0A,
  output [31:0] _0x0B,
  output [31:0] _0x0C,
  output [31:0] _0x0D,
  output [31:0] _0x0E,
  output [31:0] _0x0F
);

  wire demultiplexer_1_out1, demultiplexer_1_out2, demultiplexer_1_out3, demultiplexer_1_out4,
       demultiplexer_1_out5, demultiplexer_1_out6, demultiplexer_1_out7, demultiplexer_1_out8,
       demultiplexer_1_out9, demultiplexer_1_out10, demultiplexer_1_out11, demultiplexer_1_out12,
       demultiplexer_1_out13, demultiplexer_1_out14, demultiplexer_1_out15;
  wire [31:0] undriven, undriven_2, undriven_3, undriven_4, undriven_5, undriven_6, undriven_7, undriven_8,
       undriven_9, undriven_10, undriven_11, undriven_12, undriven_13, undriven_14, undriven_15, undriven_16;

  Demultiplexer #(.select(5), .enable("false")) demultiplexer_1 (
    .out1(demultiplexer_1_out1), .out2(demultiplexer_1_out2), .out3(demultiplexer_1_out3),
    .out4(demultiplexer_1_out4), .out5(demultiplexer_1_out5), .out6(demultiplexer_1_out6),
    .out7(demultiplexer_1_out7), .out8(demultiplexer_1_out8), .out9(demultiplexer_1_out9),
    .out10(demultiplexer_1_out10), .out11(demultiplexer_1_out11), .out12(demultiplexer_1_out12),
    .out13(demultiplexer_1_out13), .out14(demultiplexer_1_out14), .out15(demultiplexer_1_out15), .sel(SelDest));  // open: out0, out16, out17, out18, out19, out20, out21, out22, out23, out24, out25, out26, out27, out28, out29, out30, out31, in
  Register #(.width(32)) u__0x00 (.D(_0x00), .Q(_0x00), .clk(Clock));  // open: en, clr
  Register #(.width(32)) u__0x01 (.D(RFIn), .en(demultiplexer_1_out1), .Q(_0x01), .clk(Clock));  // open: clr
  Register #(.width(32)) u__0x02 (.D(RFIn), .en(demultiplexer_1_out2), .Q(_0x02), .clk(Clock));  // open: clr
  Register #(.width(32)) u__0x03 (.D(RFIn), .en(demultiplexer_1_out3), .Q(_0x03), .clk(Clock));  // open: clr
  Register #(.width(32)) u__0x04 (.D(RFIn), .en(demultiplexer_1_out4), .Q(_0x04), .clk(Clock));  // open: clr
  Register #(.width(32)) u__0x05 (.D(RFIn), .en(demultiplexer_1_out5), .Q(_0x05), .clk(Clock));  // open: clr
  Register #(.width(32)) u__0x06 (.D(RFIn), .en(demultiplexer_1_out6), .Q(_0x06), .clk(Clock));  // open: clr
  Register #(.width(32)) u__0x07 (.D(RFIn), .en(demultiplexer_1_out7), .Q(_0x07), .clk(Clock));  // open: clr
  Register #(.width(32)) u__0x08 (.D(RFIn), .en(demultiplexer_1_out8), .Q(_0x08), .clk(Clock));  // open: clr
  Register #(.width(32)) u__0x09 (.D(RFIn), .en(demultiplexer_1_out9), .Q(_0x09), .clk(Clock));  // open: clr
  Register #(.width(32)) u__0x0A (.D(RFIn), .en(demultiplexer_1_out10), .Q(_0x0A), .clk(Clock));  // open: clr
  Register #(.width(32)) u__0x0B (.D(RFIn), .en(demultiplexer_1_out11), .Q(_0x0B), .clk(Clock));  // open: clr
  Register #(.width(32)) u__0x0C (.D(RFIn), .en(demultiplexer_1_out12), .Q(_0x0C), .clk(Clock));  // open: clr
  Register #(.width(32)) u__0x0D (.D(RFIn), .en(demultiplexer_1_out13), .Q(_0x0D), .clk(Clock));  // open: clr
  Register #(.width(32)) u__0x0E (.D(RFIn), .en(demultiplexer_1_out14), .Q(_0x0E), .clk(Clock));  // open: clr
  Register #(.width(32)) u__0x0F (.D(RFIn), .en(demultiplexer_1_out15), .Q(_0x0F), .clk(Clock));  // open: clr
  Multiplexer #(.select(5), .width(32), .enable("false")) multiplexer_1 (
    .in0(_0x00), .in1(_0x01), .in2(_0x02), .in3(_0x03), .in4(_0x04), .in5(_0x05), .in6(_0x06), .in7(_0x07),
    .in8(_0x08), .in9(_0x09), .in10(_0x0A), .in11(_0x0B), .in12(_0x0C), .in13(_0x0D), .in14(_0x0E),
    .in15(_0x0F), .in16(undriven_16), .in17(undriven_15), .in18(undriven_14), .in19(undriven_13),
    .in20(undriven_12), .in21(undriven_11), .in22(undriven_10), .in23(undriven_9), .in24(undriven_8),
    .in25(undriven_7), .in26(undriven_6), .in27(undriven_5), .in28(undriven_4), .in29(undriven_3),
    .in30(undriven_2), .in31(undriven), .out(RFOpA), .sel(SelOpA));
  Multiplexer #(.select(5), .width(32), .enable("false")) multiplexer_2 (
    .in0(_0x00), .in1(_0x01), .in2(_0x02), .in3(_0x03), .in4(_0x04), .in5(_0x05), .in6(_0x06), .in7(_0x07),
    .in8(_0x08), .in9(_0x09), .in10(_0x0A), .in11(_0x0B), .in12(_0x0C), .in13(_0x0D), .in14(_0x0E),
    .in15(_0x0F), .in16(undriven_16), .in17(undriven_15), .in18(undriven_14), .in19(undriven_13),
    .in20(undriven_12), .in21(undriven_11), .in22(undriven_10), .in23(undriven_9), .in24(undriven_8),
    .in25(undriven_7), .in26(undriven_6), .in27(undriven_5), .in28(undriven_4), .in29(undriven_3),
    .in30(undriven_2), .in31(undriven), .out(RFOpB), .sel(SelOpB));

  // Other names for the same wires on the sheet: REG00[31:0] = _0x00; REG0A[31:0] = _0x0A; REG0B[31:0] = _0x0B;
  //   REG0C[31:0] = _0x0C; REG0D[31:0] = _0x0D; REG0E[31:0] = _0x0E; REG0F[31:0] = _0x0F; REG01[31:0] = _0x01;
  //   REG02[31:0] = _0x02; REG03[31:0] = _0x03; REG04[31:0] = _0x04; REG05[31:0] = _0x05; REG06[31:0] = _0x06;
  //   REG07[31:0] = _0x07; REG08[31:0] = _0x08; REG09[31:0] = _0x09
endmodule

module InstructionDecoder (
  input  [31:0] instruction,
  output Load,
  output Store,
  output LUI,
  output AUIPC,
  output JAL,
  output funct7,
  output [4:0] rs2,
  output [4:0] rs1,
  output [2:0] funct3,
  output [4:0] rd,
  output JALR,
  output [19:0] Imm20,
  output [11:0] Imm12,
  output selImmI,
  output Branch
);

  wire comparator_1_eq;

  Comparator #(.width(5)) comparator_1 (.a(instruction[6:2]), .b(5'b00100), .eq(comparator_1_eq));  // open: gt, lt
  or or_1 (selImmI, Load, Store, comparator_1_eq);
  Comparator #(.width(7)) comparator_2 (.a(7'b0000011), .b(instruction[6:0]), .eq(Load));  // open: gt, lt
  Comparator #(.width(7)) comparator_3 (.a(7'b0100011), .b(instruction[6:0]), .eq(Store));  // open: gt, lt
  Comparator #(.width(7)) comparator_4 (.a(7'b0110111), .b(instruction[6:0]), .eq(LUI));  // open: gt, lt
  Comparator #(.width(7)) comparator_5 (.a(7'b0010111), .b(instruction[6:0]), .eq(AUIPC));  // open: gt, lt
  Comparator #(.width(7)) comparator_6 (.a(7'b1101111), .b(instruction[6:0]), .eq(JAL));  // open: gt, lt
  Comparator #(.width(7)) comparator_7 (.a(7'b1100111), .b(instruction[6:0]), .eq(JALR));  // open: gt, lt
  Comparator #(.width(7)) comparator_8 (.a(7'b1100011), .b(instruction[6:0]), .eq(Branch));  // open: gt, lt

  assign funct3 = instruction[14:12];
  assign funct7 = instruction[30];
  assign Imm12 = instruction[31:20];
  assign Imm20 = instruction[31:12];
  assign rd = instruction[11:7];
  assign rs1 = instruction[19:15];
  assign rs2 = instruction[24:20];

  // Notes on the sheet:
  //   immS/funct7
endmodule

module Main (
  input  in_1,
  input  [31:0] IMIn,
  input  in_3,
  input  [3:0] RAMCtrl,
  output [31:0] IMOut
);

  wire ALUEq, ALUFunct7, ALUInf, ALUSup, and_1_out, and_2_out, and_3_out, and_4_out, AUIPC, Branch,
       BranchCond, Clock, ImmSel, JAL, JALR, Load, LUI, not_1_out, not_2_out, not_3_out, not_4_out, or_1_out,
       or_2_out, or_3_out, or_4_out, or_5_out, Store;
  wire [2:0] ALUFunct3, Funct3;
  wire [4:0] Rd, Rs1, Rs2;
  wire [7:0] multiplexer_13_out;
  wire [11:0] Imm12, multiplexer_5_out;
  wire [15:0] multiplexer_11_out;
  wire [19:0] adder_1_out, adder_2_out, adder_3_out, Imm20, multiplexer_1_out, multiplexer_3_out,
       multiplexer_12_out, Offset, PC;
  wire [23:0] multiplexer_10_out;
  wire [31:0] ALUIn1, ALUIn2, ALUOut, DMIn, DMOut, multiplexer_6_out, multiplexer_8_out,
       registerfile_1__0x00, registerfile_1__0x0a, registerfile_1__0x0b, registerfile_1__0x0c,
       registerfile_1__0x0d, registerfile_1__0x0e, registerfile_1__0x0f, registerfile_1__0x01,
       registerfile_1__0x02, registerfile_1__0x03, registerfile_1__0x04, registerfile_1__0x05,
       registerfile_1__0x06, registerfile_1__0x07, registerfile_1__0x08, registerfile_1__0x09, RFIn, RFLoad,
       RFOut2;

  // Probe on registerfile_1__0x00
  // Probe on registerfile_1__0x02
  // Probe on registerfile_1__0x04
  // Probe on registerfile_1__0x06
  // Probe on registerfile_1__0x08
  // Probe on registerfile_1__0x0a
  // Probe on registerfile_1__0x0c
  // Probe on registerfile_1__0x0e
  Register #(.width(20)) u_PC (.D(multiplexer_3_out), .Q(PC), .clk(Clock), .clr(in_3));  // open: en
  or or_1 (or_1_out, Store, Load);
  // Probe on registerfile_1__0x01
  // Probe on registerfile_1__0x03
  // Probe on registerfile_1__0x05
  // Probe on registerfile_1__0x07
  // Probe on registerfile_1__0x09
  // Probe on registerfile_1__0x0b
  // Probe on registerfile_1__0x0d
  // Probe on registerfile_1__0x0f
  RAM #(.dataWidth(32), .bus("separate")) ram_1 (
    .addr(ALUOut[7:0]), .din(DMIn), .data(DMOut), .str(Store), .sel(or_1_out), .clk(Clock), .ld(Load),
    .clr(in_1));
  Multiplexer #(.width(20), .enable("false")) multiplexer_1 (
    .in0(20'h1), .in1(Offset), .out(multiplexer_1_out), .sel(or_2_out));
  or or_2 (or_2_out, JAL, and_1_out, JALR);
  and and_1 (and_1_out, BranchCond, Branch);
  not not_1 (not_1_out, ALUEq);
  not not_2 (not_2_out, ALUInf);
  not not_3 (not_3_out, ALUInf);
  Clock u_Clock (.out(Clock));
  Adder #(.width(20)) adder_1 (.a(PC), .b(multiplexer_1_out), .out(adder_1_out), .cin(1'b0));  // open: cout
  Adder #(.width(20)) adder_2 (.a(PC), .b(Offset), .out(adder_2_out), .cin(1'b0));  // open: cout
  Multiplexer #(.select(3), .enable("false")) multiplexer_2 (
    .in0(ALUEq), .in1(not_1_out), .in2(1'b0), .in3(1'b0), .in4(ALUInf), .in5(not_2_out), .in6(ALUInf),
    .in7(not_3_out), .out(BranchCond), .sel(Funct3));
  RegisterFile registerfile_1 (
    .RFIn(RFIn), .Clock(Clock), .RFOpA(ALUIn1), .RFOpB(RFOut2), .SelDest(Rd), .SelOpA(Rs1), .SelOpB(Rs2),
    ._0x01(registerfile_1__0x01), ._0x02(registerfile_1__0x02), ._0x03(registerfile_1__0x03),
    ._0x04(registerfile_1__0x04), ._0x05(registerfile_1__0x05), ._0x06(registerfile_1__0x06),
    ._0x07(registerfile_1__0x07), ._0x08(registerfile_1__0x08), ._0x09(registerfile_1__0x09),
    ._0x0A(registerfile_1__0x0a), ._0x0B(registerfile_1__0x0b), ._0x0C(registerfile_1__0x0c),
    ._0x0D(registerfile_1__0x0d), ._0x0E(registerfile_1__0x0e), ._0x0F(registerfile_1__0x0f),
    ._0x00(registerfile_1__0x00));
  and and_2 (and_2_out, Imm20[19], or_3_out);
  Multiplexer #(.width(20), .enable("false")) multiplexer_3 (
    .in0(adder_1_out), .in1(adder_2_out), .out(multiplexer_3_out), .sel(and_2_out));
  or or_3 (or_3_out, JAL, and_3_out, JALR);
  and and_3 (and_3_out, BranchCond, Branch);
  // Probe on ALUIn1
  // Probe on ALUIn2
  // Probe on ALUFunct3
  ALU alu_1 (
    .OpA(ALUIn1), .OpB(ALUIn2), .Res(ALUOut), .AluSup(ALUSup), .AluEq(ALUEq), .AluInf(ALUInf),
    .func3(ALUFunct3), .func7(ALUFunct7));
  // Probe on ALUOut
  RAM #(.addrWidth(20), .dataWidth(32), .bus("separate")) ram_2 (
    .addr(PC), .din(IMIn), .data(IMOut), .str(RAMCtrl[3]), .sel(RAMCtrl[2]), .clk(Clock), .ld(RAMCtrl[1]),
    .clr(RAMCtrl[0]));
  InstructionDecoder instructiondecoder_1 (
    .funct7(ALUFunct7), .rs2(Rs2), .rs1(Rs1), .funct3(Funct3), .rd(Rd), .selImmI(ImmSel),
    .instruction(IMOut), .Imm12(Imm12), .JALR(JALR), .JAL(JAL), .AUIPC(AUIPC), .LUI(LUI), .Load(Load),
    .Store(Store), .Imm20(Imm20), .Branch(Branch));
  Multiplexer #(.width(3), .enable("false")) multiplexer_4 (
    .in0(Funct3), .in1(3'b000), .out(ALUFunct3), .sel(or_4_out));
  or or_4 (or_4_out, Load, Store);
  Multiplexer #(.width(12), .enable("false")) multiplexer_5 (
    .in0(Imm12), .in1({Imm12[11:5], Rd}), .out(multiplexer_5_out), .sel(Store));
  Multiplexer #(.width(32), .enable("false")) multiplexer_6 (
    .in0(ALUOut), .in1({Imm20, {12{1'b0}}}), .out(multiplexer_6_out), .sel(LUI));
  Multiplexer #(.width(32), .enable("false")) multiplexer_7 (
    .in0(RFOut2), .in1({{20{1'b0}}, multiplexer_5_out}), .out(ALUIn2), .sel(ImmSel));
  Multiplexer #(.width(32), .enable("false")) multiplexer_8 (
    .in0(multiplexer_6_out), .in1(RFLoad), .out(multiplexer_8_out), .sel(Load));
  Adder #(.width(20)) adder_3 (.a(20'h20), .b(PC), .out(adder_3_out));  // open: cin, cout
  Multiplexer #(.width(32), .enable("false")) multiplexer_9 (
    .in0(multiplexer_8_out), .in1({{12{1'b0}}, adder_3_out}), .out(RFIn), .sel(or_5_out));
  or or_5 (or_5_out, JAL, JALR);
  Multiplexer #(.width(24), .enable("false")) multiplexer_10 (
    .in0({24{1'b0}}), .in1({24{1'b1}}), .out(multiplexer_10_out), .sel(DMOut[7]));
  Multiplexer #(.width(16), .enable("false")) multiplexer_11 (
    .in0({16{1'b0}}), .in1({16{1'b1}}), .out(multiplexer_11_out), .sel(DMOut[15]));
  Multiplexer #(.width(20), .enable("false")) multiplexer_12 (
    .in0({Imm20[19], Imm20[8:0], Imm20[9], Imm20[18:10]}), .in1({{8{1'b0}}, Imm12}),
    .out(multiplexer_12_out), .sel(JALR));
  Multiplexer #(.width(8), .enable("false")) multiplexer_13 (
    .in0({8{1'b0}}), .in1({8{1'b1}}), .out(multiplexer_13_out), .sel(and_4_out));
  and and_4 (and_4_out, not_4_out, Imm20[19]);
  not not_4 (not_4_out, Funct3[1]);
  Multiplexer #(.width(20), .enable("false")) multiplexer_14 (
    .in0(multiplexer_12_out), .in1({multiplexer_13_out, Imm12[11], Rd[0], Imm12[10:5], Rd[4:1]}),
    .out(Offset), .sel(Branch));
  Multiplexer #(.select(3), .width(32), .enable("false")) multiplexer_15 (
    .in0({multiplexer_10_out, DMOut[7:0]}), .in1({multiplexer_11_out, DMOut[15:0]}), .in2(DMOut),
    .in3({32{1'b0}}), .in4({{24{1'b0}}, DMOut[7:0]}), .in5({{16{1'b0}}, DMOut[15:0]}), .in6({32{1'b0}}),
    .in7({32{1'b0}}), .out(RFLoad), .sel(Funct3));
  Multiplexer #(.select(3), .width(32), .enable("false")) multiplexer_16 (
    .in0({{24{1'b0}}, RFOut2[7:0]}), .in1({{16{1'b0}}, RFOut2[15:0]}), .in2(RFOut2), .in3({32{1'b0}}),
    .in4({32{1'b0}}), .in5({32{1'b0}}), .in6({32{1'b0}}), .in7({32{1'b0}}), .out(DMIn), .sel(Funct3));

  // Other names for the same wires on the sheet: OffsetSign = Imm20[19]; DMAddr[7:0] = ALUOut[7:0];
  //   Funct7 = ALUFunct7; RFOut1[31:0] = ALUIn1

  // Notes on the sheet:
  //   MainCircuitProcessor
  //   Ctrl+t or click for simulation :
  //   RegisterFile
  //   DataMemory
  //   ProgramCounter
  //   InstructionDecoder
  //   ALU
  //   InstructionMemory
  //   ALU IN/OUT
  //   Load
  //   Store
  //   Jump/Branch
endmodule
